# Fritzing sketch hareket_sensoru (saved by Fritzing 0.8.7b)
breadboards: 1

parts:
  J1 = Piezo Speaker
  R1 = Resistor [tolerance=±5% resistance=220 package=THT]
  LED1 = LED - 5mm [color="Red (633nm)" package="5 mm [THT]"]
  Q1 = NPN-Transistor [package="TO92 [THT]"]
  Eleman1 = Arduino Uno (Rev3)
  R2 = Resistor [tolerance=±5% resistance=220 package=THT]

nets:
  N1: J1.pin1, Eleman1.D12/MISO
  N2: J1.pin2, R2.Pin_1
  N3: R1.Pin_0, LED1.cathode
  N4: R1.Pin_1, Q1.E, Q1.C, Eleman1.GND, R2.Pin_0
  N5: LED1.anode, Eleman1.D7
  N6: Q1.B, Eleman1.D8
