# Fritzing sketch isik_ldr (saved by Fritzing 0.8.7b)
breadboards: 1

parts:
  Eleman1 = Arduino Uno (Rev3)
  R1 = Resistor [tolerance=±5% resistance=220 package=THT]
  R2 = PHOTOCELL [package=photocell]
  R3 = Resistor [tolerance=±5% resistance=1k package=THT]
  LED1 = LED - 5mm [color="Red (633nm)" package="5 mm [THT]"]

nets:
  N1: Eleman1.A0, R2.P$1, R3.Pin_1
  N2: Eleman1.D3_PWM, R1.Pin_1
  N3: Eleman1.5V, R2.P$2
  N4: Eleman1.GND, R3.Pin_0, LED1.cathode
  N5: R1.Pin_0, LED1.anode
