# Fritzing sketch lcd_yazi (saved by Fritzing 0.8.7b)
breadboards: 1

parts:
  Eleman1 = Arduino Uno (Rev3)
  Q1 = PNP-Transistor [package="SOT-23 [SMD]"]
  U1 = LCD-16X2 [package=lcd-16x2]

nets:
  N1: Eleman1.D11_PWM/MOSI, U1.E
  N2: Eleman1.D12/MISO, U1.RS
  N3: Eleman1.D2, U1.DB7
  N4: Eleman1.D3_PWM, U1.DB6
  N5: Eleman1.D4, U1.DB5
  N6: Eleman1.D5_PWM, U1.DB4
  5V: Eleman1.5V, Q1.1, U1.VDD, U1.A
  GND: Eleman1.GND, Q1.2, U1.VSS, U1.R_W, U1.K
  N7: Q1.0, U1.VO
