# Fritzing sketch servo_motor (saved by Fritzing 0.8.7b)
breadboards: 1

parts:
  Eleman1 = Arduino Uno (Rev3)
  J2 = Basic Servo

nets:
  N1: Eleman1.D9_PWM, J2.pulse
  5V: Eleman1.5V, J2.vcc
  GND: Eleman1.GND, J2.gnd
