# Fritzing sketch rain (saved by Fritzing 0.8.7b)
breadboards: 1

parts:
  J1 = Piezo Speaker
  Eleman1 = Arduino Uno (Rev3)
  R2 = Resistor [tolerance=±5% resistance=220 package=THT]
  Q1 = PNP-Transistor [package="SOT-23 [SMD]"]

nets:
  N1: J1.pin1, Eleman1.D12/MISO
  N2: J1.pin2, R2.Pin_1
  N3: Eleman1.A0, Q1.1
  N4: Eleman1.5V, Q1.0
  N5: Eleman1.GND, R2.Pin_0, Q1.2
